# Fritzing sketch arduino lcd rtc 3x shift 16x led (saved by Fritzing 0.9.3b)
breadboards: 2

parts:
  Onderdeel1 = Arduino Uno (Rev3)
  LCD1 = LCD screen
  U1 = 74HC595 [package="DIP16 [THT]"]
  U2 = 74HC595 [package="DIP16 [THT]"]
  U3 = 74HC595 [package="DIP16 [THT]"]
  R1 = Resistor [tolerance=±5% resistance=220 package=THT]
  R2 = Resistor [tolerance=±5% resistance=220 package=THT]
  R3 = Resistor [tolerance=±5% resistance=220 package=THT]
  R4 = Resistor [tolerance=±5% resistance=220 package=THT]
  R5 = Resistor [tolerance=±5% resistance=220 package=THT]
  R6 = Resistor [tolerance=±5% resistance=220 package=THT]
  R7 = Resistor [tolerance=±5% resistance=220 package=THT]
  R8 = Resistor [tolerance=±5% resistance=220 package=THT]
  R9 = Resistor [tolerance=±5% resistance=220 package=THT]
  R10 = Resistor [tolerance=±5% resistance=220 package=THT]
  R11 = Resistor [tolerance=±5% resistance=220 package=THT]
  R12 = Resistor [tolerance=±5% resistance=220 package=THT]
  R13 = Resistor [tolerance=±5% resistance=220 package=THT]
  R14 = Resistor [tolerance=±5% resistance=220 package=THT]
  R15 = Resistor [tolerance=±5% resistance=220 package=THT]
  R16 = Resistor [tolerance=±5% resistance=220 package=THT]
  LED1 = LED - 3mm [color="Red (633nm)" package="3 mm [THT]"]
  LED2 = LED - 3mm [color="Red (633nm)" package="3 mm [THT]"]
  LED5 = LED - 3mm [color="Red (633nm)" package="3 mm [THT]"]
  LED3 = LED - 3mm [color="Red (633nm)" package="3 mm [THT]"]
  LED4 = LED - 3mm [color="Red (633nm)" package="3 mm [THT]"]
  LED6 = LED - 3mm [color="Red (633nm)" package="3 mm [THT]"]
  LED7 = LED - 3mm [color="Red (633nm)" package="3 mm [THT]"]
  LED8 = LED - 3mm [color="Red (633nm)" package="3 mm [THT]"]
  LED9 = LED - 3mm [color="Red (633nm)" package="3 mm [THT]"]
  LED10 = LED - 3mm [color="Red (633nm)" package="3 mm [THT]"]
  LED11 = LED - 3mm [color="Red (633nm)" package="3 mm [THT]"]
  LED12 = LED - 3mm [color="Red (633nm)" package="3 mm [THT]"]
  LED13 = LED - 3mm [color="Red (633nm)" package="3 mm [THT]"]
  LED14 = LED - 3mm [color="Red (633nm)" package="3 mm [THT]"]
  LED15 = LED - 3mm [color="Red (633nm)" package="3 mm [THT]"]
  LED16 = LED - 3mm [color="Red (633nm)" package="3 mm [THT]"]
  R17 = Trimmer Potentiometer [maximum_resistance=10kΩ package=THT]
  R18 = Resistor [tolerance=±5% resistance=220 package=THT]
  IC1 = DS1302 [package="DIP8 [THT]"]
  BAT1 = Battery Holders [package=battcom_20mm_pth]
  Y1 = CRYSTAL [package=crystal-32khz-smd]
  LED17 = LED - 5mm [color="Red (633nm)" package="5 mm [THT]"]
  LED18 = LED - 5mm [color="Red (633nm)" package="5 mm [THT]"]
  U4 = RF-LINK_TX [package=rf-link_tx]
  ANT1 = Antenna

nets:
  N1: Onderdeel1.A1, U1.DS
  N2: Onderdeel1.A2, U1.SH_CP, U2.SH_CP
  N3: Onderdeel1.A3, U1.ST_CP, U2.ST_CP
  N4: Onderdeel1.D9_PWM, IC1.I/O_-_SPI_Data_In/Out
  N5: Onderdeel1.D10_PWM/SS, IC1.CE_-_Chip_Enable
  N6: Onderdeel1.D11_PWM/MOSI, U4.DATA
  N7: Onderdeel1.D2, U3.DS
  N8: Onderdeel1.D3_PWM, LCD1.E, U3.ST_CP
  N9: Onderdeel1.D4, U3.SH_CP
  N10: Onderdeel1.D5_PWM, LED17.anode
  N11: Onderdeel1.D6_PWM, LED18.anode
  VCC: Onderdeel1.5V, LCD1.LED+, U1.MR, U1.VCC, U2.MR, U2.Q0, U3.MR, U3.VCC, R17.leg2, R18.Pin_0, IC1.+V, U4.+5V
  GND: Onderdeel1.GND, LCD1.VSS, LCD1.R/W, LCD1.LED-, U1.GND, U1.OE, U2.GND, U2.OE, U3.GND, U3.OE, LED1.cathode, LED2.cathode, LED5.cathode, LED3.cathode, LED4.cathode, LED6.cathode, LED7.cathode, LED8.cathode, LED9.cathode, LED10.cathode, LED11.cathode, LED12.cathode, LED13.cathode, LED14.cathode, LED15.cathode, LED16.cathode, R17.leg1, IC1.0V, LED17.cathode, LED18.cathode, U4.GND
  N12: LCD1.V0, R17.wiper
  N13: LCD1.RS, U3.Q2
  N14: LCD1.DB4, U3.Q3
  N15: LCD1.DB5, U3.Q4
  N16: LCD1.DB6, U3.Q5
  N17: LCD1.DB7, U3.Q6
  N18: U1.Q1, R1.Pin_0
  N19: U1.Q2, R2.Pin_0
  N20: U1.Q3, R3.Pin_0
  N21: U1.Q4, R4.Pin_0
  N22: U1.Q5, R5.Pin_0
  N23: U1.Q6, R6.Pin_0
  N24: U1.Q7, R7.Pin_0
  N25: U1.Q0, R8.Pin_0
  N26: U2.Q1, R9.Pin_0
  N27: U2.Q2, R10.Pin_0
  N28: U2.Q3, R11.Pin_0
  N29: U2.Q4, R12.Pin_0
  N30: U2.Q5, R13.Pin_0
  N31: U2.Q6, R14.Pin_0
  N32: U2.Q7, R15.Pin_0
  N33: U2.DS, R16.Pin_0
  N34: R1.Pin_1, LED1.anode
  N35: R2.Pin_1, LED2.anode
  N36: R3.Pin_1, LED3.anode
  N37: R4.Pin_1, LED4.anode
  N38: R5.Pin_1, LED5.anode
  N39: R6.Pin_1, LED6.anode
  N40: R7.Pin_1, LED7.anode
  N41: R8.Pin_1, LED8.anode
  N42: R9.Pin_1, LED9.anode
  N43: R10.Pin_1, LED10.anode
  N44: R11.Pin_1, LED11.anode
  N45: R12.Pin_1, LED12.anode
  N46: R13.Pin_1, LED13.anode
  N47: R14.Pin_1, LED14.anode
  N48: R15.Pin_1, LED15.anode
  N49: R16.Pin_1, LED16.anode
  N50: IC1.X1_-_Crystal, Y1.1
  N51: IC1.X2_-_Crystal, Y1.2
  N52: IC1.Vbat_-_Backup_Supply, BAT1.+
  N53: U4.ANT, ANT1.antenna_lead

// code stored in the sketch: lcd rtc 3x shift 16xled werkend.ino


/*
  ShiftLCD Library - Hello World

  Demonstrates the use a 16x2 LCD display.  The ShiftLCD library works with
  all LCD displays that are compatible with the Hitachi HD44780 driver.
  There are many of them out there, and you can usually tell them by the
  16-pin interface.

  This sketch prints "Hello World!" to the LCD
  and shows the number of seconds since reset.

  The circuit:

  ---Shift Register 74HC595---
  SR SER - Pin 14 to Arduino pin PD2
  SR RCK - Pin 12 to Arduino pin PD3 and (LCD E 1602 Pin 6)
  SR SCK - Pin 11 to Arduino pin PD4
  SR GND - Pin  8 to Ground
  SR VCC - Pin 16 to +5v
  SR OE - Pin 13 to Ground
  SR SCLR - Pin 10 to +5v
  -----Shift Reg to LCD--------
  SR QG - Pin 6 to D7 (LCD 1602 Pin 14)
  SR QF - Pin 5  to D6 (LCD 1602 Pin 13)
  SR QE - Pin 4  to D5 (LCD 1602 Pin 12)
  SR QD - Pin 3  to D4 (LCD 1602 Pin 11)
  SR QC - Pin 2  to LCD RS (LCD 1602 Pin 4)
  -----LCD HD44780-------------
  Vss to Ground    (LCD 1602 Pin 1)
  Vdd to +5V       (LCD 1602 Pin 2)
  Vo  to 10k Wiper (LCD 1602 Pin 3)
  R/W to Ground    (LCD 1602 Pin 5)
  LEDA  to +5v     (LCD 1602 Pin 15)
  Gnd to LEDK via 330 Ohm resistor  (LCD 1602 Pin 16)

  The schematic at this link is:
  http://code.google.com/p/arduinoshiftreglcd/ see
  the last schematic labled "Latched shiftregister"

*/
#include <TimeLib.h>
#include <TimeAlarms.h>


#include <virtuabotixRTC.h> //Libraries needed
virtuabotixRTC myRTC(8, 9, 10); //If you change the wiring change the pins here also

#include <LiquidCrystal_SR.h>

#define SHIFT_DATA A1
#define SHIFT_LATCH A2
#define SHIFT_CLK A3

#define  DATAPIN  2
#define  CLOCKPIN 4
#define  STROBEPIN 3

#define STROOM 5
#define KOFFIE 6


LiquidCrystal_SR lcd(DATAPIN, CLOCKPIN, STROBEPIN);


int allon = 0b1111111111111111;  //  1 alles aan
int alloff = 0b0000000000000000;  //  2 alles uit
int address3 = 0b0101010101010101;  //  3 om en om
int address4 = 0b1010101010101010;  //  4 om en om

int LEDa1 = 0b0000000100000000;  //  1 led 1 aan
int LEDa2 = 0b0000001000000000;  //  2 led 2 aan
int LEDa3 = 0b0000010000000000;  //  3 led 3 aan
int LEDa4 = 0b0000100000000000;  //  4 led 4 aan
int LEDa5 = 0b0001000000000000;  //  5 led 5 aan
int LEDa6 = 0b0010000000000000;  //  6 led 6 aan
int LEDa7 = 0b0100000000000000;  //  7 led 7 aan
int LEDa8 = 0b1000000000000000;  //  8 led 8 aan

int LEDb1 = 0b0000000000000001;  //  9 led 9 aan
int LEDb2 = 0b0000000000000010;  //  10 led 10 aan
int LEDb3 = 0b0000000000000100;  //  11 led 11 aan
int LEDb4 = 0b0000000000001000;  //  12 led 12 aan
int LEDb5 = 0b0000000000010000;  //  13 led 13 aan
int LEDb6 = 0b0000000000100000;  //  14 led 14 aan
int LEDb7 = 0b0000000001000000;  //  15 led 15 aan
int LEDb8 = 0b0000000010000000;  //  16 led 16 aan



void setup() {

  pinMode(STROOM, OUTPUT);
  pinMode(KOFFIE, OUTPUT);
  pinMode(A1, OUTPUT); // data
  pinMode(A2, OUTPUT); // latch
  pinMode(A3, OUTPUT); // clock

  lcd.begin(16, 2);
  lcd.home ();
  myRTC.setDS1302Time(00, 41, 15, 5, 03, 4, 2021);

  setTime(15, 41, 00, 4, 03, 21); // set time

  // creeer alarmen
  Alarm.alarmRepeat(15, 41, 30, POWER);      // 8:30 Stroom aan
  Alarm.alarmRepeat(15, 41, 50, COFFEE);     // 8:30,5 is koffie start
  Alarm.alarmRepeat(15, 42, 00, POWEROFF);   //8:31 Stroom uit

  Alarm.alarmRepeat(15, 42, 10, LEDA1);  //  1
  Alarm.alarmRepeat(15, 42, 15, LEDA2);  //  2
  Alarm.alarmRepeat(15, 42, 20, LEDA3);  //  3
  Alarm.alarmRepeat(15, 42, 25, LEDA4);  //  4
  Alarm.alarmRepeat(15, 42, 30, LEDA5);  //  5
  Alarm.alarmRepeat(15, 42, 35, LEDA6);  //  6
  Alarm.alarmRepeat(15, 42, 40, LEDA7);  //  7
  Alarm.alarmRepeat(15, 42, 45, LEDA8);  //  8

  Alarm.alarmRepeat(15, 42, 50, LEDB1);  //  9
  Alarm.alarmRepeat(15, 42, 55, LEDB2);  //  10
  Alarm.alarmRepeat(15, 43, 00, LEDB3);  //  11
  Alarm.alarmRepeat(15, 43, 05, LEDB4);  //  12
  Alarm.alarmRepeat(15, 43, 10, LEDB5);  //  13
  Alarm.alarmRepeat(15, 43, 15, LEDB6);  //  14
  Alarm.alarmRepeat(15, 43, 20, LEDB7);  //  15
  Alarm.alarmRepeat(15, 43, 25, LEDB8);  //  16

  Alarm.alarmRepeat(15, 43, 30, LEDON);  //  ALLES AAN
  Alarm.alarmRepeat(15, 43, 35, LEDOFF); //  ALLES UIT



}

void loop() {
  digitalClockDisplay();
  Alarm.delay(1000);
  lcd.clear();
}


//functies voor alarmen
void POWER() {
  lcd.clear();
  lcd.setCursor(0, 1);
  lcd.print("De stroom = AAN");
  digitalWrite(STROOM, HIGH);
  delay(5000);
}

void COFFEE() {
  lcd.clear();
  lcd.setCursor(0, 1);
  lcd.print("De koffie loopt");
  digitalWrite(KOFFIE, HIGH);
  delay(5000);
  digitalWrite(KOFFIE, LOW);
}

void POWEROFF() {
  lcd.clear();
  lcd.setCursor(0, 1);
  lcd.print("De stroom = UIT");
  lcd.setCursor(0, 1);
  lcd.print("koffie is klaar");
  digitalWrite(STROOM, LOW);
  delay(5000);
}

void LEDA1() {

  lcd.clear();
  lcd.setCursor(0, 1);
  lcd.print("LED-1");
  delay(1000);
  shiftOut(SHIFT_DATA, SHIFT_CLK, MSBFIRST, (LEDa1 >> 8)); // Load first 8 bits
  shiftOut(SHIFT_DATA, SHIFT_CLK, MSBFIRST, LEDa1);        // Load second 8
  digitalWrite(SHIFT_LATCH, LOW);
  digitalWrite(SHIFT_LATCH, HIGH);
  digitalWrite(SHIFT_LATCH, LOW);
  delay(1000);

}

void LEDA2() {
  lcd.clear();
  lcd.setCursor(0, 1);
  lcd.print("LED-2");
  delay(1000);
  shiftOut(SHIFT_DATA, SHIFT_CLK, MSBFIRST, (LEDa2 >> 8)); // Load first 8 bits
  shiftOut(SHIFT_DATA, SHIFT_CLK, MSBFIRST, LEDa2);        // Load second 8
  digitalWrite(SHIFT_LATCH, LOW);
  digitalWrite(SHIFT_LATCH, HIGH);
  digitalWrite(SHIFT_LATCH, LOW);


}

void LEDA3() {
  lcd.clear();
  lcd.setCursor(0, 1);
  lcd.print("LED-3");
  delay(1000);
  shiftOut(SHIFT_DATA, SHIFT_CLK, MSBFIRST, (LEDa3 >> 8)); // Load first 8 bits
  shiftOut(SHIFT_DATA, SHIFT_CLK, MSBFIRST, LEDa3);        // Load second 8
  digitalWrite(SHIFT_LATCH, LOW);
  digitalWrite(SHIFT_LATCH, HIGH);
  digitalWrite(SHIFT_LATCH, LOW);
  delay(100);
}

void LEDA4() {
  lcd.clear();
  lcd.setCursor(0, 1);
  lcd.print("LED-4");
  delay(1000);
  shiftOut(SHIFT_DATA, SHIFT_CLK, MSBFIRST, (LEDa4 >> 8)); // Load first 8 bits
  shiftOut(SHIFT_DATA, SHIFT_CLK, MSBFIRST, LEDa4);        // Load second 8
  digitalWrite(SHIFT_LATCH, LOW);
  digitalWrite(SHIFT_LATCH, HIGH);
  digitalWrite(SHIFT_LATCH, LOW);
  delay(100);
}

void LEDA5() {
  lcd.clear();
  lcd.setCursor(0, 1);
  lcd.print("LED-5");
  delay(1000);
  shiftOut(SHIFT_DATA, SHIFT_CLK, MSBFIRST, (LEDa5 >> 8)); // Load first 8 bits
  shiftOut(SHIFT_DATA, SHIFT_CLK, MSBFIRST, LEDa5);        // Load second 8
  digitalWrite(SHIFT_LATCH, LOW);
  digitalWrite(SHIFT_LATCH, HIGH);
  digitalWrite(SHIFT_LATCH, LOW);
  delay(100);
}

void LEDA6() {
  lcd.clear();
  lcd.setCursor(0, 1);
  lcd.print("LED-6");
  delay(1000);
  shiftOut(SHIFT_DATA, SHIFT_CLK, MSBFIRST, (LEDa6 >> 8)); // Load first 8 bits
  shiftOut(SHIFT_DATA, SHIFT_CLK, MSBFIRST, LEDa6);        // Load second 8
  digitalWrite(SHIFT_LATCH, LOW);
  digitalWrite(SHIFT_LATCH, HIGH);
  digitalWrite(SHIFT_LATCH, LOW);
  delay(100);
}

void LEDA7() {
  lcd.clear();
  lcd.setCursor(0, 1);
  lcd.print("LED-7");
  delay(1000);
  shiftOut(SHIFT_DATA, SHIFT_CLK, MSBFIRST, (LEDa7 >> 8)); // Load first 8 bits
  shiftOut(SHIFT_DATA, SHIFT_CLK, MSBFIRST, LEDa7);        // Load second 8
  digitalWrite(SHIFT_LATCH, LOW);
  digitalWrite(SHIFT_LATCH, HIGH);
  digitalWrite(SHIFT_LATCH, LOW);
  delay(100);
}

void LEDA8() {
  lcd.clear();
  lcd.setCursor(0, 1);
  lcd.print("LED-8");
  delay(1000);
  shiftOut(SHIFT_DATA, SHIFT_CLK, MSBFIRST, (LEDa8 >> 8)); // Load first 8 bits
  shiftOut(SHIFT_DATA, SHIFT_CLK, MSBFIRST, LEDa8);        // Load second 8
  digitalWrite(SHIFT_LATCH, LOW);
  digitalWrite(SHIFT_LATCH, HIGH);
  digitalWrite(SHIFT_LATCH, LOW);
  delay(100);
}

void LEDB1() {
  lcd.clear();
  lcd.setCursor(0, 1);
  lcd.print("LED-9");
  delay(1000);
  shiftOut(SHIFT_DATA, SHIFT_CLK, MSBFIRST, (LEDb1 >> 8)); // Load first 8 bits
  shiftOut(SHIFT_DATA, SHIFT_CLK, MSBFIRST, LEDb1);        // Load second 8
  digitalWrite(SHIFT_LATCH, LOW);
  digitalWrite(SHIFT_LATCH, HIGH);
  digitalWrite(SHIFT_LATCH, LOW);
  delay(100);
}

void LEDB2() {
  lcd.clear();
  lcd.setCursor(0, 1);
  lcd.print("LED-10");
  delay(1000);
  shiftOut(SHIFT_DATA, SHIFT_CLK, MSBFIRST, (LEDb2 >> 8)); // Load first 8 bits
  shiftOut(SHIFT_DATA, SHIFT_CLK, MSBFIRST, LEDb2);        // Load second 8
  digitalWrite(SHIFT_LATCH, LOW);
  digitalWrite(SHIFT_LATCH, HIGH);
  digitalWrite(SHIFT_LATCH, LOW);
  delay(100);
}

void LEDB3() {
  lcd.clear();
  lcd.setCursor(0, 1);
  lcd.print("LED-11");
  delay(1000);
  shiftOut(SHIFT_DATA, SHIFT_CLK, MSBFIRST, (LEDb3 >> 8)); // Load first 8 bits
  shiftOut(SHIFT_DATA, SHIFT_CLK, MSBFIRST, LEDb3);        // Load second 8
  digitalWrite(SHIFT_LATCH, LOW);
  digitalWrite(SHIFT_LATCH, HIGH);
  digitalWrite(SHIFT_LATCH, LOW);
  delay(100);
}

void LEDB4() {
  lcd.clear();
  lcd.setCursor(0, 1);
  lcd.print("LED-12");
  delay(1000);
  shiftOut(SHIFT_DATA, SHIFT_CLK, MSBFIRST, (LEDb4 >> 8)); // Load first 8 bits
  shiftOut(SHIFT_DATA, SHIFT_CLK, MSBFIRST, LEDb4);        // Load second 8
  digitalWrite(SHIFT_LATCH, LOW);
  digitalWrite(SHIFT_LATCH, HIGH);
  digitalWrite(SHIFT_LATCH, LOW);
  delay(100);
}

void LEDB5() {
  lcd.clear();
  lcd.setCursor(0, 1);
  lcd.print("LED-13");
  delay(1000);
  shiftOut(SHIFT_DATA, SHIFT_CLK, MSBFIRST, (LEDb5 >> 8)); // Load first 8 bits
  shiftOut(SHIFT_DATA, SHIFT_CLK, MSBFIRST, LEDb5);        // Load second 8
  digitalWrite(SHIFT_LATCH, LOW);
  digitalWrite(SHIFT_LATCH, HIGH);
  digitalWrite(SHIFT_LATCH, LOW);
  delay(100);
}

void LEDB6() {
  lcd.clear();
  lcd.setCursor(0, 1);
  lcd.print("LED-14");
  delay(1000);
  shiftOut(SHIFT_DATA, SHIFT_CLK, MSBFIRST, (LEDb6 >> 8)); // Load first 8 bits
  shiftOut(SHIFT_DATA, SHIFT_CLK, MSBFIRST, LEDb6);        // Load second 8
  digitalWrite(SHIFT_LATCH, LOW);
  digitalWrite(SHIFT_LATCH, HIGH);
  digitalWrite(SHIFT_LATCH, LOW);
  delay(100);
}

void LEDB7() {
  lcd.clear();
  lcd.setCursor(0, 1);
  lcd.print("LED-15");
  delay(1000);
  shiftOut(SHIFT_DATA, SHIFT_CLK, MSBFIRST, (LEDb7 >> 8)); // Load first 8 bits
  shiftOut(SHIFT_DATA, SHIFT_CLK, MSBFIRST, LEDb7);        // Load second 8
  digitalWrite(SHIFT_LATCH, LOW);
  digitalWrite(SHIFT_LATCH, HIGH);
  digitalWrite(SHIFT_LATCH, LOW);
  delay(100);
}

void LEDB8() {
  lcd.clear();
  lcd.setCursor(0, 1);
  lcd.print("LED-16");
  delay(1000);
  shiftOut(SHIFT_DATA, SHIFT_CLK, MSBFIRST, (LEDb8 >> 8)); // Load first 8 bits
  shiftOut(SHIFT_DATA, SHIFT_CLK, MSBFIRST, LEDb8);        // Load second 8
  digitalWrite(SHIFT_LATCH, LOW);
  digitalWrite(SHIFT_LATCH, HIGH);
  digitalWrite(SHIFT_LATCH, LOW);
  delay(100);
}

void LEDON() {
  lcd.clear();
  lcd.setCursor(0, 1);
  lcd.print("ALLES AAN");
  delay(1000);
  shiftOut(SHIFT_DATA, SHIFT_CLK, MSBFIRST, (allon >> 8)); // Load first 8 bits
  shiftOut(SHIFT_DATA, SHIFT_CLK, MSBFIRST, allon);        // Load second 8 bits

  digitalWrite(SHIFT_LATCH, LOW);
  digitalWrite(SHIFT_LATCH, HIGH);
  digitalWrite(SHIFT_LATCH, LOW);
  delay(100);
}

void LEDOFF() {
  lcd.clear();
  lcd.setCursor(0, 1);
  lcd.print("ALLES UIT");

  shiftOut(SHIFT_DATA, SHIFT_CLK, MSBFIRST, (alloff >> 8)); // Load first 8 bits
  shiftOut(SHIFT_DATA, SHIFT_CLK, MSBFIRST, alloff);        // Load second 8 bits

  digitalWrite(SHIFT_LATCH, LOW);
  digitalWrite(SHIFT_LATCH, HIGH);
  digitalWrite(SHIFT_LATCH, LOW);
  delay(1000);
}


void digitalClockDisplay() {

  lcd.clear(); //Here after clearing the LCD we take the time from the module and print it on the screen with usual LCD functions
  myRTC.updateTime();

  lcd.setCursor(0, 0); lcd.print('B');
  lcd.setCursor(1, 0); lcd.print('o');
  lcd.setCursor(2, 0); lcd.print('r');
  lcd.setCursor(3, 0); lcd.print('e');
  lcd.setCursor(4, 0); lcd.print('n');
  lcd.setCursor(5, 0); lcd.print('t');

  lcd.setCursor(8, 0);  if (myRTC.hours < 10) lcd.print('0'); lcd.print(myRTC.hours);
  lcd.setCursor(10, 0); lcd.print(':');
  lcd.setCursor(11, 0); if (myRTC.minutes < 10) lcd.print('0'); lcd.print(myRTC.minutes);
  lcd.setCursor(13, 0); lcd.print(':');
  lcd.setCursor(14, 0); if (myRTC.seconds < 10) lcd.print('0'); lcd.print(myRTC.seconds);

  lcd.setCursor(0, 1); if (myRTC.dayofmonth < 10) lcd.print('0'); lcd.print(myRTC.dayofmonth);
  lcd.setCursor(2, 1); lcd.print('/');
  lcd.setCursor(3, 1); lcd.print(myRTC.month);
  lcd.setCursor(4, 1); lcd.print('/');
  lcd.setCursor(5, 1); lcd.print(myRTC.year);

}
